# Fritzing sketch Memory_Hunter_v1.5_Wiring Schematic (saved by Fritzing 0.9.3b)

parts:
  Memory_Hunter_v1_5 = Arduino Uno (Rev3) - ICSP
  S-RED = Round Pushbutton
  S-Yellow = Round Pushbutton
  S-Green = Round Pushbutton
  S-Blue = Round Pushbutton
  part = smd LED [color="Red (633nm)" package="1206 [SMD]"]
  part_2 = smd LED [color="Green (570nm)" package="1206 [SMD]"]
  part_3 = smd LED [color="Yellow (595nm)" package="1206 [SMD]"]
  part_4 = smd LED [color="Blue (525nm)" package="1206 [SMD]"]
  R-Blue = Resistor [tolerance=±5% resistance=220 package="0402 [SMD]"]
  R-Red = Resistor [tolerance=±5% resistance=220 package="0402 [SMD]"]
  R-Yellow = Resistor [tolerance=±5% resistance=220 package="0402 [SMD]"]
  R-Green = Resistor [tolerance=±5% resistance=220 package="0402 [SMD]"]
  Buzzer = Piezo Speaker
  U1 = WS2812 RGB LED strip
  R-WS2812 = Resistor [tolerance=±5% resistance=220 package="0402 [SMD]"]

nets:
  5V: Memory_Hunter_v1_5.5V, U1.VCC
  GND: Memory_Hunter_v1_5.GND, S-RED.leg0, S-Yellow.leg1, S-Green.leg0, S-Blue.leg1, part.cathode, part_2.cathode, part_3.cathode, part_4.cathode, Buzzer.pin1, U1.GND
  N1: Memory_Hunter_v1_5.D8, S-Yellow.leg0
  N2: Memory_Hunter_v1_5.D9_PWM, R-Green.Pin_0
  N3: Memory_Hunter_v1_5.D10_PWM/SS, R-Blue.Pin_1
  N4: Memory_Hunter_v1_5.D11_PWM/MOSI, R-Yellow.Pin_1
  N5: Memory_Hunter_v1_5.D12/MISO, Buzzer.pin2
  N6: Memory_Hunter_v1_5.D13/SCK, R-WS2812.Pin_1
  N7: Memory_Hunter_v1_5.D4, S-RED.leg1
  N8: Memory_Hunter_v1_5.D5_PWM, S-Green.leg1
  N9: Memory_Hunter_v1_5.D6_PWM, R-Red.Pin_0
  N10: Memory_Hunter_v1_5.D7, S-Blue.leg0
  N11: part.anode, R-Red.Pin_1
  N12: part_2.anode, R-Green.Pin_1
  N13: part_3.anode, R-Yellow.Pin_0
  N14: part_4.anode, R-Blue.Pin_0
  N15: U1.DIN, R-WS2812.Pin_0

custom parts:
  WS2812 RGB LED strip: WS2812 strip
